# Fritzing sketch A06 (saved by Fritzing 0.9.6b)
breadboards: 1

parts:
  M1 = Freenove MicroBit GPIO extension board
  LED1 = LED - 5mm [color="Red (633nm)" current=0.030 package="5 mm [THT]"]
  R1 = Resistor [tolerance=±5% power=0.25 resistance=1k package=THT]
  R2 = Resistor [tolerance=±5% power=0.25 resistance=220 package=THT]
  R3 = Resistor [tolerance=±5% power=0.25 resistance=1k package=THT]
  S3 = Momentary Switch [package=ksa_sealed_tac_switch]

nets:
  N1: M1.GND, LED1.cathode, S3.3, S3.4
  N2: M1.3.3V, R1.Pin_1
  N3: M1.P0, R3.Pin_1
  N4: M1.P1, R2.Pin_1
  N5: LED1.anode, R2.Pin_0
  N6: R1.Pin_0, R3.Pin_0, S3.1, S3.2
