# Fritzing sketch A07 (saved by Fritzing 0.9.6b)
breadboards: 1

parts:
  M1 = Freenove MicroBit GPIO extension board
  R1 = Resistor [tolerance=±5% power=0.25 resistance=220 package=THT]
  R2 = Resistor [tolerance=±5% power=0.25 resistance=220 package=THT]
  R3 = Resistor [tolerance=±5% power=0.25 resistance=220 package=THT]
  LED2 = RGB LED - (4 legs) [package="5 mm [THT]"]

nets:
  N1: M1.3.3V, LED2.common_anode
  N2: M1.P0, R1.Pin_1
  N3: M1.P1, R2.Pin_1
  N4: M1.P2, R3.Pin_1
  N5: R1.Pin_0, LED2.blue_cathode
  N6: R2.Pin_0, LED2.green_cathode
  N7: R3.Pin_0, LED2.red_cathode
